// Logisim project Processor.circ as structural Verilog: 18 circuits, main circuit Processor
module Processor (
  input  Reset,
  input  [3:0] Display_Address
);

  wire alu_1_is, alu_1_is_2, branch_lock_unit_1_invalidatesignal, branch_unit_1_isbranchtaken, Call, Clock,
       control_unit_1_isimmediate, flags_1_flags_e, flags_1_flags_gt, not_1_out, O2, O3, O11, O12, or_1_out,
       St, Wb;
  wire [1:0] O21;
  wire [1:1] ma_rw_latch_1_out_12, O22;
  wire [3:0] ex_ma_latch_1_out_12, ma_rw_latch_1_out_11_2, multiplexer_9_out, multiplexer_10_out,
       multiplexer_13_out, of_ex_latch_1_out_18, register_file_1_displayd, register_file_1_displayd_2,
       register_file_1_displayd_3, register_file_1_displayd_4, register_file_1_displayd_5;
  wire [4:0] if_of_latch_1_out_8_2;
  wire [6:0] of_ex_latch_1_out_18_2;
  wire [7:0] control_unit_1_isubranch;
  wire [12:0] control_unit_1_alusignals, of_ex_latch_1_out_19;
  wire [26:0] if_of_latch_1_out_8;
  wire [31:0] A1, A2, A3, A4, adder_1_out, adder_2_out, adder_3_out, alu_1_aluresult, bit_extender_1_out,
       calculate_immediate_1_immx, ex_ma_latch_1_out_8, ex_ma_latch_1_out_9, ex_ma_latch_1_out_10,
       ex_ma_latch_1_out_11, if_of_latch_1_out_7, ma_rw_latch_1_out_8, ma_rw_latch_1_out_9,
       ma_rw_latch_1_out_10, ma_rw_latch_1_out_11, memory_unit_1_ldresult, multiplexer_1_out,
       multiplexer_2_out, multiplexer_3_out, multiplexer_4_out, multiplexer_5_out, multiplexer_6_out,
       multiplexer_7_out, multiplexer_8_out, multiplexer_11_out, multiplexer_12_out, of_ex_latch_1_out_12,
       of_ex_latch_1_out_13, of_ex_latch_1_out_14, of_ex_latch_1_out_15, of_ex_latch_1_out_16,
       of_ex_latch_1_out_17, PC_q, register_file_1_readd1, register_file_1_readd2, rom_1_data, shifter_1_out;
  wire [31:20] register_file_1_displayd_6;

  Forwarding_Unit forwarding_unit_1 (
    .OF_instruction(A1), .EX_instruction(A2), .MA_instruction(A3), .RW_instruction(A4), .RW_OF_1(O11),
    .RW_EX_1(O21[0]), .RW_MA(O3), .RW_OF_2(O12), .RW_EX_2(O2), .MA_EX_1(O21[1]), .MA_EX_2(O22[1]));
  not not_1 (not_1_out, St);
  Register #(.width(32), .trigger("falling")) PC (
    .D(multiplexer_1_out), .en(not_1_out), .Q(PC_q), .clk(Clock), .clr(Reset));
  IF_OF_Latch if_of_latch_1 (
    .in_1(PC_q), .in_2(rom_1_data), .out_7(if_of_latch_1_out_7),
    .out_8({if_of_latch_1_out_8_2, if_of_latch_1_out_8}), .in_4(Clock), .in_6(Reset),
    .in_3(branch_lock_unit_1_invalidatesignal), .out_9(A1), .Stall(St));
  OF_EX_Latch of_ex_latch_1 (
    .in_1(if_of_latch_1_out_7), .in_2(adder_3_out), .in_3(multiplexer_11_out), .in_4(multiplexer_5_out),
    .in_5(multiplexer_4_out), .in_6({if_of_latch_1_out_8_2, if_of_latch_1_out_8}),
    .in_7(control_unit_1_isubranch), .out_12(of_ex_latch_1_out_12), .out_13(of_ex_latch_1_out_13),
    .out_14(of_ex_latch_1_out_14), .out_15(of_ex_latch_1_out_15), .out_16(of_ex_latch_1_out_16),
    .out_17(of_ex_latch_1_out_17),
    .out_18({of_ex_latch_1_out_18[3], of_ex_latch_1_out_18_2[6], of_ex_latch_1_out_18[2:0], of_ex_latch_1_out_18_2[2:0]}),
    .in_10(Clock), .in_11(Reset), .in_8(control_unit_1_alusignals), .out_19(of_ex_latch_1_out_19),
    .in_9(or_1_out), .out_20(A2));
  EX_MA_Latch ex_ma_latch_1 (
    .in_2(alu_1_aluresult), .in_3(multiplexer_7_out), .in_4(of_ex_latch_1_out_17),
    .in_5(of_ex_latch_1_out_18), .out_9(ex_ma_latch_1_out_9), .out_10(ex_ma_latch_1_out_10),
    .out_11(ex_ma_latch_1_out_11), .out_12(ex_ma_latch_1_out_12), .in_6(Clock), .in_7(Reset),
    .in_1(of_ex_latch_1_out_12), .out_8(ex_ma_latch_1_out_8), .out_13(A3));
  MA_RW_Latch ma_rw_latch_1 (
    .in_1(ex_ma_latch_1_out_8), .in_2(ex_ma_latch_1_out_9), .in_3(memory_unit_1_ldresult),
    .in_4(ex_ma_latch_1_out_11), .in_5({ex_ma_latch_1_out_12[3:2], ex_ma_latch_1_out_12[0]}),
    .out_8(ma_rw_latch_1_out_8), .out_9(ma_rw_latch_1_out_9), .out_10(ma_rw_latch_1_out_10),
    .out_11({ma_rw_latch_1_out_11[31:26], ma_rw_latch_1_out_11_2, ma_rw_latch_1_out_11[21:0]}),
    .out_12({Wb, ma_rw_latch_1_out_12[1], Call}), .in_6(Clock), .in_7(Reset), .out_13(A4));
  Multiplexer #(.width(32), .enable("false")) multiplexer_1 (
    .in0(adder_1_out), .in1(multiplexer_2_out), .out(multiplexer_1_out), .sel(branch_unit_1_isbranchtaken));
  assign bit_extender_1_out = {{5{if_of_latch_1_out_8[26]}}, if_of_latch_1_out_8};  // Bit_Extender bit_extender_1
  Adder #(.width(32)) adder_1 (.a(32'h4), .b(PC_q), .out(adder_1_out));  // open: cin, cout
  Shifter #(.width(32)) shifter_1 (.in(bit_extender_1_out), .\dist (5'b00010), .out(shifter_1_out));
  ALU alu_1 (
    .A(multiplexer_12_out), .B(multiplexer_6_out), .ALUsignals(of_ex_latch_1_out_19),
    .aluResult(alu_1_aluresult), .is(alu_1_is), .is_2(alu_1_is_2));
  Adder #(.width(32)) adder_2 (.a(ma_rw_latch_1_out_8), .b(32'h4), .out(adder_2_out));  // open: cin, cout
  ROM #(.addrWidth(24), .dataWidth(32)) rom_1 (.addr(PC_q[25:2]), .data(rom_1_data));  // open: sel
  Calculate_Immediate calculate_immediate_1 (.imm(if_of_latch_1_out_8[17:0]), .immx(calculate_immediate_1_immx));
  Adder #(.width(32)) adder_3 (.a(shifter_1_out), .b(if_of_latch_1_out_7), .out(adder_3_out));  // open: cin, cout
  Multiplexer #(.width(32), .enable("false")) multiplexer_2 (
    .in0(of_ex_latch_1_out_13), .in1(multiplexer_12_out), .out(multiplexer_2_out),
    .sel(of_ex_latch_1_out_18_2[6]));
  Memory_Unit memory_unit_1 (
    .MAR(ex_ma_latch_1_out_9), .ldResult(memory_unit_1_ldresult), .MDR(multiplexer_8_out),
    .isSt(ex_ma_latch_1_out_12[1]), .isLd(ex_ma_latch_1_out_12[2]), .Clock(Clock), .Reset(Reset));
  Multiplexer #(.select(2), .width(32), .enable("false")) multiplexer_3 (
    .in0(ma_rw_latch_1_out_9), .in1(ma_rw_latch_1_out_10), .in2(adder_2_out), .out(multiplexer_3_out),
    .sel({Call, ma_rw_latch_1_out_12[1]}));  // open: in3
  Clock u_Clock (.out(Clock));
  Multiplexer #(.width(32), .enable("false")) multiplexer_4 (
    .in0(register_file_1_readd2), .in1(multiplexer_3_out), .out(multiplexer_4_out), .sel(O12));
  Multiplexer #(.width(32), .enable("false")) multiplexer_5 (
    .in0(multiplexer_4_out), .in1(calculate_immediate_1_immx), .out(multiplexer_5_out),
    .sel(control_unit_1_isimmediate));
  Multiplexer #(.select(2), .width(32), .enable("false")) multiplexer_6 (
    .in0(of_ex_latch_1_out_15), .in1(multiplexer_3_out), .in2(ex_ma_latch_1_out_9),
    .in3(ex_ma_latch_1_out_9), .out(multiplexer_6_out), .sel({O22[1], O2}));
  Flags flags_1 (
    .isCmp(of_ex_latch_1_out_19[0]), .is(alu_1_is), .is_2(alu_1_is_2), .flags_GT(flags_1_flags_gt),
    .flags_E(flags_1_flags_e));
  Multiplexer #(.width(32), .enable("false")) multiplexer_7 (
    .in0(of_ex_latch_1_out_16), .in1(multiplexer_3_out), .out(multiplexer_7_out), .sel(O2));
  Multiplexer #(.width(32), .enable("false")) multiplexer_8 (
    .in0(ex_ma_latch_1_out_10), .in1(multiplexer_3_out), .out(multiplexer_8_out), .sel(O3));
  Hex_Digit_Display hex_digit_display_1 (.value(register_file_1_displayd_6[31:28]));  // open: dp
  Multiplexer #(.width(4), .enable("false")) multiplexer_9 (
    .in0(if_of_latch_1_out_8[17:14]), .in1(if_of_latch_1_out_8[25:22]), .out(multiplexer_9_out),
    .sel(control_unit_1_isubranch[4]));
  Hex_Digit_Display hex_digit_display_2 (.value(register_file_1_displayd_6[27:24]));  // open: dp
  Multiplexer #(.width(4), .enable("false")) multiplexer_10 (
    .in0(if_of_latch_1_out_8[21:18]), .in1(4'b1111), .out(multiplexer_10_out),
    .sel(control_unit_1_isubranch[6]));
  Register_File register_file_1 (
    .ReadA1(multiplexer_10_out), .ReadA2(multiplexer_9_out), .WriteE(Wb), .WriteD(multiplexer_3_out),
    .ReadD1(register_file_1_readd1), .ReadD2(register_file_1_readd2), .Clock(Clock), .Reset(Reset),
    .DisplayD({register_file_1_displayd_6, register_file_1_displayd_5, register_file_1_displayd_4, register_file_1_displayd_3, register_file_1_displayd_2, register_file_1_displayd}),
    .DisplayA(Display_Address), .WriteA(multiplexer_13_out));
  Multiplexer #(.width(32), .enable("false")) multiplexer_11 (
    .in0(register_file_1_readd1), .in1(multiplexer_3_out), .out(multiplexer_11_out), .sel(O11));
  Multiplexer #(.select(2), .width(32), .enable("false")) multiplexer_12 (
    .in0(of_ex_latch_1_out_14), .in1(multiplexer_3_out), .in2(ex_ma_latch_1_out_9),
    .in3(ex_ma_latch_1_out_9), .out(multiplexer_12_out), .sel(O21));
  Branch_Unit branch_unit_1 (
    .isBeq(of_ex_latch_1_out_18_2[2]), .isUBranch(of_ex_latch_1_out_18_2[0]), .flags_E(flags_1_flags_e),
    .isBgt(of_ex_latch_1_out_18_2[1]), .flags_GT(flags_1_flags_gt),
    .isBranchTaken(branch_unit_1_isbranchtaken));
  Hex_Digit_Display hex_digit_display_3 (.value(register_file_1_displayd_6[23:20]));  // open: dp
  Hex_Digit_Display hex_digit_display_4 (.value(register_file_1_displayd_5));  // open: dp
  Hex_Digit_Display hex_digit_display_5 (.value(register_file_1_displayd_4));  // open: dp
  Control_Unit control_unit_1 (
    .isSt(control_unit_1_isubranch[4]), .isLd(control_unit_1_isubranch[5]),
    .isBeq(control_unit_1_isubranch[2]), .isBgt(control_unit_1_isubranch[1]),
    .isRet(control_unit_1_isubranch[6]), .I_bit(if_of_latch_1_out_8[26]),
    .isImmediate(control_unit_1_isimmediate), .opcode(if_of_latch_1_out_8_2),
    .isWb(control_unit_1_isubranch[7]), .isUbranch(control_unit_1_isubranch[0]),
    .isCall(control_unit_1_isubranch[3]), .ALUsignals(control_unit_1_alusignals));
  Hex_Digit_Display hex_digit_display_6 (.value(register_file_1_displayd_3));  // open: dp
  Hex_Digit_Display hex_digit_display_7 (.value(register_file_1_displayd));  // open: dp
  Hex_Digit_Display hex_digit_display_8 (.value(register_file_1_displayd_2));  // open: dp
  Multiplexer #(.width(4), .enable("false")) multiplexer_13 (
    .in0(ma_rw_latch_1_out_11_2), .in1(4'b1111), .out(multiplexer_13_out), .sel(Call));
  // Probe on {register_file_1_displayd_6, register_file_1_displayd_5, register_file_1_displayd_4, register_file_1_displayd_3, register_file_1_displayd_2, register_file_1_displayd}
  or or_1 (or_1_out, branch_lock_unit_1_invalidatesignal, St);
  Data_Lock_Unit data_lock_unit_1 (.OF_instruction(A1), .EX_instruction(A2), .Stall(St));
  Branch_Lock_Unit branch_lock_unit_1 (
    .invalidateSignal(branch_lock_unit_1_invalidatesignal), .isBranchTaken(branch_unit_1_isbranchtaken));

  // Other names for the same wires on the sheet: O22[0] = O2

  // Notes on the sheet:
  //   isBranchTaken
  //   pc+4
  //   ALUsignals
  //   B
  //   aluResult
  //   pc
  //   branchTarget
  //   offset
  //   pc
  //   branchTarget
  //   isBranchTaken
  //   A
  //   ALU
  //   aluResult
  //   MAR
  //   Memory
  //   Unit
  //   ldResult
  //   Instruction Memory
  //   contents of rom_1 (hex, n*v repeats v):
  //   4c000000 4c40000c 7c400000 4c400007 7c400004 4c40000b 7c400008 4c400009 7c40000c 4c400003 7c400010
  //   4c40000f 7c400014 4c800000 4cc00005 14cc0004 108c000 9800001d 90000000 48c10000 d100004 75480000
  //   758c0000 75d00000 28090000 88000012 28194000 8800000a 281d8000 8800000b 7d500000 7dc80000 4880004
  //   75480000 d100004 75d00000 97fffff4 4880004 75480000 97fffff1 d100004 75d00000 97ffffee 7d4c0000
  //   7d880000 a0000000 28090000 8800000f fb80010 7cb80000 7d380008 7ff8000c 9fffffdf 7cb80004 74b80000
  //   9ffffff7 74b80004 4880004 75380008 9ffffff3 77f8000c 7b80010 a0000000
  //   calc immx
  //   imm
  //   isRet
  //   is>
  //   is=
  //   MDR
  //   data
  //   immx
  //   op2
  //   Flags
  //   isCmp
  //   op2
  //   isLd
  //   isSt
  //   isLd
  //   isCall
  //   5 STAGE PROCESSOR
  //   instruction
  //   rs1
  //   rs2
  //   rd
  //   isSt
  //   Register
  //   File
  //   op2
  //   isImmediate
  //   flags(GT)
  //   flags(E)
  //   data
  //   data
  //   isRet
  //   isWb
  //   E
  //   address
  //   A
  //   data
  //   D
  //   op1
  //   Branch
  //   Unit
  //   opcode
  //   I bit
  //   isBeq
  //   isBgt
  //   isUBranch
  //   Display Register
  //   CONTROL
  //   UNIT
  //   isWb
  //   data
  //   isWb
  //   isWb
  //   isCall
  //   isCall
  //   rd
endmodule

module Control_Unit (
  input  I_bit,
  input  [4:0] opcode,
  output isSt,
  output isLd,
  output isBeq,
  output isBgt,
  output isRet,
  output isImmediate,
  output isWb,
  output isUbranch,
  output isCall,
  output [12:0] ALUsignals
);

  wire and_6_out, and_7_out, and_8_out, and_9_out, and_10_out, and_12_out, and_13_out, nand_1_out;

  nand nand_1 (nand_1_out, opcode[0], opcode[1]);
  and and_1 (isSt, opcode[0], opcode[1], opcode[2], opcode[3], ~opcode[4]);  // AND_Gate
  and and_2 (isLd, ~opcode[0], opcode[1], opcode[2], opcode[3], ~opcode[4]);  // AND_Gate
  and and_3 (isBeq, ~opcode[0], ~opcode[1], ~opcode[2], ~opcode[3], opcode[4]);  // AND_Gate
  and and_4 (isBgt, opcode[0], ~opcode[1], ~opcode[2], ~opcode[3], opcode[4]);  // AND_Gate
  and and_5 (isRet, ~opcode[0], ~opcode[1], opcode[2], ~opcode[3], opcode[4]);  // AND_Gate
  and and_6 (and_6_out, opcode[0], ~opcode[1], opcode[2], ~opcode[4]);  // AND_Gate
  and and_7 (and_7_out, opcode[0], opcode[2], opcode[3], ~opcode[4]);  // AND_Gate
  and and_8 (and_8_out, opcode[4], nand_1_out);
  and and_9 (and_9_out, opcode[1], ~opcode[2], ~opcode[3], opcode[4]);  // AND_Gate
  and and_10 (and_10_out, ~opcode[0], ~opcode[1], opcode[2], ~opcode[3], opcode[4]);  // AND_Gate
  and and_11 (isCall, opcode[0], opcode[1], ~opcode[2], ~opcode[3], opcode[4]);  // AND_Gate
  and and_12 (and_12_out, ~opcode[0], ~opcode[1], ~opcode[2], ~opcode[3], ~opcode[4]);  // AND_Gate
  and and_13 (and_13_out, opcode[1], opcode[2], opcode[3], ~opcode[4]);  // AND_Gate
  and isSub (ALUsignals[2], opcode[0], ~opcode[1], ~opcode[2], ~opcode[3], ~opcode[4]);  // AND_Gate
  and isCmp (ALUsignals[0], opcode[0], ~opcode[1], opcode[2], ~opcode[3], ~opcode[4]);  // AND_Gate
  and isMul (ALUsignals[3], ~opcode[0], opcode[1], ~opcode[2], ~opcode[3], ~opcode[4]);  // AND_Gate
  and isDiv (ALUsignals[4], opcode[0], opcode[1], ~opcode[2], ~opcode[3], ~opcode[4]);  // AND_Gate
  and isMod (ALUsignals[5], ~opcode[0], ~opcode[1], opcode[2], ~opcode[3], ~opcode[4]);  // AND_Gate
  and isLsl (ALUsignals[7], ~opcode[0], opcode[1], ~opcode[2], opcode[3], ~opcode[4]);  // AND_Gate
  and isLsr (ALUsignals[8], opcode[0], opcode[1], ~opcode[2], opcode[3], ~opcode[4]);  // AND_Gate
  and isAsr (ALUsignals[9], ~opcode[0], ~opcode[1], opcode[2], opcode[3], ~opcode[4]);  // AND_Gate
  and isOr (ALUsignals[12], opcode[0], opcode[1], opcode[2], ~opcode[3], ~opcode[4]);  // AND_Gate
  and isAnd (ALUsignals[11], ~opcode[0], opcode[1], opcode[2], ~opcode[3], ~opcode[4]);  // AND_Gate
  and isNot (ALUsignals[10], ~opcode[0], ~opcode[1], ~opcode[2], opcode[3], ~opcode[4]);  // AND_Gate
  and isMov (ALUsignals[6], opcode[0], ~opcode[1], ~opcode[2], opcode[3], ~opcode[4]);  // AND_Gate
  or or_1 (isUbranch, and_9_out, and_10_out);
  or isAdd (ALUsignals[1], and_12_out, and_13_out);
  nor nor_1 (isWb, and_6_out, and_7_out, and_8_out);

  assign isImmediate = I_bit;

  // Notes on the sheet:
  //   op1
  //   op2
  //   op3
  //   op4
  //   op5
endmodule

module Register_File (
  input  Clock,
  input  Reset,
  input  [31:0] WriteD,
  input  [3:0] ReadA1,
  input  WriteE,
  input  [3:0] WriteA,
  input  [3:0] ReadA2,
  input  [3:0] DisplayA,
  output [31:0] ReadD1,
  output [31:0] ReadD2,
  output [31:0] DisplayD
);

  wire demultiplexer_1_out0, demultiplexer_1_out1, demultiplexer_1_out2, demultiplexer_1_out3,
       demultiplexer_1_out4, demultiplexer_1_out5, demultiplexer_1_out6, demultiplexer_1_out7,
       demultiplexer_1_out8, demultiplexer_1_out9, demultiplexer_1_out10, demultiplexer_1_out11,
       demultiplexer_1_out12, demultiplexer_1_out13, demultiplexer_1_out14, demultiplexer_1_out15,
       multiplexer_2_out, or_1_out, or_2_out;
  wire [31:0] multiplexer_1_out, r0_q, r1_q, r2_q, r3_q, r4_q, r5_q, r6_q, r7_q, r8_q, r9_q, r10_q, r11_q,
       r12_q, r13_q, r14_q, r15_q;

  Demultiplexer #(.select(4), .disabled(0), .enable("false")) demultiplexer_1 (
    .out0(demultiplexer_1_out0), .out1(demultiplexer_1_out1), .out2(demultiplexer_1_out2),
    .out3(demultiplexer_1_out3), .out4(demultiplexer_1_out4), .out5(demultiplexer_1_out5),
    .out6(demultiplexer_1_out6), .out7(demultiplexer_1_out7), .out8(demultiplexer_1_out8),
    .out9(demultiplexer_1_out9), .out10(demultiplexer_1_out10), .out11(demultiplexer_1_out11),
    .out12(demultiplexer_1_out12), .out13(demultiplexer_1_out13), .out14(demultiplexer_1_out14),
    .out15(demultiplexer_1_out15), .in(WriteE), .sel(WriteA));
  Multiplexer #(.width(32), .enable("false")) multiplexer_1 (
    .in0(WriteD), .in1(32'h3fffffc), .out(multiplexer_1_out), .sel(Reset));
  or or_1 (or_1_out, demultiplexer_1_out14, Reset);
  or or_2 (or_2_out, Clock, Reset);
  Multiplexer #(.enable("false")) multiplexer_2 (.in0(or_2_out), .out(multiplexer_2_out), .sel(1'b0));  // open: in1
  Register #(.width(32)) r0 (.D(WriteD), .en(demultiplexer_1_out0), .Q(r0_q), .clk(Clock), .clr(Reset));
  Register #(.width(32)) r1 (.D(WriteD), .en(demultiplexer_1_out1), .Q(r1_q), .clk(Clock), .clr(Reset));
  Register #(.width(32)) r2 (.D(WriteD), .en(demultiplexer_1_out2), .Q(r2_q), .clk(Clock), .clr(Reset));
  Register #(.width(32)) r3 (.D(WriteD), .en(demultiplexer_1_out3), .Q(r3_q), .clk(Clock), .clr(Reset));
  Register #(.width(32)) r4 (.D(WriteD), .en(demultiplexer_1_out4), .Q(r4_q), .clk(Clock), .clr(Reset));
  Register #(.width(32)) r5 (.D(WriteD), .en(demultiplexer_1_out5), .Q(r5_q), .clk(Clock), .clr(Reset));
  Register #(.width(32)) r6 (.D(WriteD), .en(demultiplexer_1_out6), .Q(r6_q), .clk(Clock), .clr(Reset));
  Register #(.width(32)) r7 (.D(WriteD), .en(demultiplexer_1_out7), .Q(r7_q), .clk(Clock), .clr(Reset));
  Register #(.width(32)) r8 (.D(WriteD), .en(demultiplexer_1_out8), .Q(r8_q), .clk(Clock), .clr(Reset));
  Register #(.width(32)) r9 (.D(WriteD), .en(demultiplexer_1_out9), .Q(r9_q), .clk(Clock), .clr(Reset));
  Register #(.width(32)) r10 (.D(WriteD), .en(demultiplexer_1_out10), .Q(r10_q), .clk(Clock), .clr(Reset));
  Register #(.width(32)) r11 (.D(WriteD), .en(demultiplexer_1_out11), .Q(r11_q), .clk(Clock), .clr(Reset));
  Register #(.width(32)) r12 (.D(WriteD), .en(demultiplexer_1_out12), .Q(r12_q), .clk(Clock), .clr(Reset));
  Register #(.width(32)) r13 (.D(WriteD), .en(demultiplexer_1_out13), .Q(r13_q), .clk(Clock), .clr(Reset));
  Register #(.width(32)) r14 (.D(multiplexer_1_out), .en(or_1_out), .Q(r14_q), .clk(multiplexer_2_out));  // open: clr
  Register #(.width(32)) r15 (.D(WriteD), .en(demultiplexer_1_out15), .Q(r15_q), .clk(Clock), .clr(Reset));
  Multiplexer #(.select(4), .width(32), .disabled(0), .enable("false")) multiplexer_3 (
    .in0(r0_q), .in1(r1_q), .in2(r2_q), .in3(r3_q), .in4(r4_q), .in5(r5_q), .in6(r6_q), .in7(r7_q),
    .in8(r8_q), .in9(r9_q), .in10(r10_q), .in11(r11_q), .in12(r12_q), .in13(r13_q), .in14(r14_q),
    .in15(r15_q), .out(ReadD1), .sel(ReadA1));
  Multiplexer #(.select(4), .width(32), .disabled(0), .enable("false")) multiplexer_4 (
    .in0(r0_q), .in1(r1_q), .in2(r2_q), .in3(r3_q), .in4(r4_q), .in5(r5_q), .in6(r6_q), .in7(r7_q),
    .in8(r8_q), .in9(r9_q), .in10(r10_q), .in11(r11_q), .in12(r12_q), .in13(r13_q), .in14(r14_q),
    .in15(r15_q), .out(ReadD2), .sel(ReadA2));
  Multiplexer #(.select(4), .width(32), .disabled(0), .enable("false")) multiplexer_5 (
    .in0(r0_q), .in1(r1_q), .in2(r2_q), .in3(r3_q), .in4(r4_q), .in5(r5_q), .in6(r6_q), .in7(r7_q),
    .in8(r8_q), .in9(r9_q), .in10(r10_q), .in11(r11_q), .in12(r12_q), .in13(r13_q), .in14(r14_q),
    .in15(r15_q), .out(DisplayD), .sel(DisplayA));
endmodule

module ALU (
  input  [31:0] A,
  input  [31:0] B,
  input  [12:0] ALUsignals,
  output [31:0] aluResult,
  output is,
  output is_2
);

  wire [31:0] adder_1_out, and_1_out, divider_1_out, divider_1_rem, multiplier_1_out, not_1_out, or_1_out,
       shifter_1_out, shifter_2_out, shifter_3_out, subtractor_1_out;

  Adder #(.width(32)) adder_1 (.a(A), .b(B), .out(adder_1_out));  // open: cin, cout
  Subtractor #(.width(32)) subtractor_1 (.a(A), .b(B), .out(subtractor_1_out));  // open: bin, bout
  Multiplier #(.width(32)) multiplier_1 (.a(A), .b(B), .out(multiplier_1_out));  // open: cin, cout
  Divider #(.width(32)) divider_1 (.a(A), .b(B), .out(divider_1_out), .rem(divider_1_rem));  // open: upper
  Comparator #(.width(32)) comparator_1 (.a(A), .b(B), .gt(is), .eq(is_2));  // open: lt
  Shifter #(.width(32)) shifter_1 (.in(A), .\dist (B[4:0]), .out(shifter_1_out));
  Shifter #(.width(32), .shift("lr")) shifter_2 (.in(A), .\dist (B[4:0]), .out(shifter_2_out));
  Shifter #(.width(32), .shift("ar")) shifter_3 (.in(A), .\dist (B[4:0]), .out(shifter_3_out));
  assign not_1_out = ~B;  // NOT_Gate not_1, 32 bits wide
  assign and_1_out = A & B;  // AND_Gate and_1, 32 bits wide
  assign or_1_out = A | B;  // OR_Gate or_1, 32 bits wide
  assign aluResult = ALUsignals[1] ? adder_1_out : 32'bz;  // Controlled_Buffer controlled_buffer_1
  assign aluResult = ALUsignals[2] ? subtractor_1_out : 32'bz;  // Controlled_Buffer controlled_buffer_2
  assign aluResult = ALUsignals[3] ? multiplier_1_out : 32'bz;  // Controlled_Buffer controlled_buffer_3
  assign aluResult = ALUsignals[4] ? divider_1_out : 32'bz;  // Controlled_Buffer controlled_buffer_4
  assign aluResult = ALUsignals[5] ? divider_1_rem : 32'bz;  // Controlled_Buffer controlled_buffer_5
  assign aluResult = ALUsignals[6] ? B : 32'bz;  // Controlled_Buffer controlled_buffer_6
  assign aluResult = ALUsignals[7] ? shifter_1_out : 32'bz;  // Controlled_Buffer controlled_buffer_7
  assign aluResult = ALUsignals[8] ? shifter_2_out : 32'bz;  // Controlled_Buffer controlled_buffer_8
  assign aluResult = ALUsignals[9] ? shifter_3_out : 32'bz;  // Controlled_Buffer controlled_buffer_9
  assign aluResult = ALUsignals[10] ? not_1_out : 32'bz;  // Controlled_Buffer controlled_buffer_10
  assign aluResult = ALUsignals[11] ? and_1_out : 32'bz;  // Controlled_Buffer controlled_buffer_11
  assign aluResult = ALUsignals[12] ? or_1_out : 32'bz;  // Controlled_Buffer controlled_buffer_12

  // Notes on the sheet:
  //   add
  //   sub
  //   mul
  //   div
  //   cmp
  //   lsr
  //   mod
  //   lsl
  //   asr
endmodule

module Flags (
  input  isCmp,
  input  is,
  input  is_2,
  output flags_GT,
  output flags_E
);

  D_Flip_Flop #(.trigger("high")) d_ff_1 (.clk(isCmp), .D(is), .Q(flags_GT));  // open: Qn, preset, en, reset
  D_Flip_Flop #(.trigger("high")) d_ff_2 (.clk(isCmp), .D(is_2), .Q(flags_E));  // open: Qn, preset, en, reset
endmodule

module Branch_Unit (
  input  isUBranch,
  input  isBeq,
  input  flags_E,
  input  isBgt,
  input  flags_GT,
  output isBranchTaken
);

  wire and_1_out, and_2_out;

  and and_1 (and_1_out, isBeq, flags_E);
  and and_2 (and_2_out, isBgt, flags_GT);
  or or_1 (isBranchTaken, isUBranch, and_1_out, and_2_out);
endmodule

module Memory_Unit (
  input  [31:0] MAR,
  input  isLd,
  input  [31:0] MDR,
  input  isSt,
  input  Clock,
  input  Reset,
  output [31:0] ldResult
);

  RAM #(.addrWidth(24), .dataWidth(32), .bus("separate")) ram_1 (
    .addr(MAR[25:2]), .din(MDR), .data(ldResult), .str(isSt), .clk(Clock), .ld(isLd), .clr(Reset));  // open: sel
endmodule

module Calculate_Immediate (
  input  [17:0] imm,
  output [31:0] immx
);

  wire [31:0] bit_extender_1_out, bit_extender_2_out, shifter_1_out;

  assign bit_extender_1_out = {{16{1'b0}}, imm[15:0]};  // Bit_Extender bit_extender_1
  assign bit_extender_2_out = {{16{imm[15]}}, imm[15:0]};  // Bit_Extender bit_extender_2
  Shifter #(.width(32)) shifter_1 (.in(bit_extender_1_out), .\dist (5'b10000), .out(shifter_1_out));
  Multiplexer #(.select(2), .width(32), .enable("false")) multiplexer_1 (
    .in0(bit_extender_2_out), .in1(bit_extender_1_out), .in2(shifter_1_out), .out(immx), .sel(imm[17:16]));  // open: in3

  // Notes on the sheet:
  //   modifier bits
  //   high
  //   default
  //   unsigned
endmodule

module IF_OF_Latch (
  input  [31:0] in_1,
  input  [31:0] in_2,
  input  in_3,
  input  in_4,
  input  Stall,
  input  in_6,
  output [31:0] out_7,
  output [31:0] out_8,
  output [31:0] out_9
);

  wire not_1_out;
  wire [31:0] multiplexer_1_out;

  Multiplexer #(.width(32), .enable("false")) multiplexer_1 (
    .in0(in_2), .in1(32'h68000000), .out(multiplexer_1_out), .sel(in_3));
  not not_1 (not_1_out, Stall);
  Register #(.width(32), .trigger("falling")) register_1 (.D(in_1), .en(not_1_out), .Q(out_7), .clk(in_4), .clr(in_6));
  Register #(.width(32), .trigger("falling")) register_2 (
    .D(multiplexer_1_out), .en(not_1_out), .Q(out_8), .clk(in_4), .clr(in_6));

  assign out_9 = out_8;

  // Notes on the sheet:
  //   IF-OF LATCH
endmodule

module OF_EX_Latch (
  input  [31:0] in_1,
  input  [31:0] in_2,
  input  [31:0] in_3,
  input  [31:0] in_4,
  input  [31:0] in_5,
  input  [31:0] in_6,
  input  [7:0] in_7,
  input  [12:0] in_8,
  input  in_9,
  input  in_10,
  input  in_11,
  output [31:0] out_12,
  output [31:0] out_13,
  output [31:0] out_14,
  output [31:0] out_15,
  output [31:0] out_16,
  output [31:0] out_17,
  output [7:0] out_18,
  output [12:0] out_19,
  output [31:0] out_20
);

  wire [7:0] multiplexer_2_out;
  wire [12:0] multiplexer_3_out;
  wire [31:0] multiplexer_1_out;

  Multiplexer #(.width(32), .enable("false")) multiplexer_1 (
    .in0(in_6), .in1(32'h68000000), .out(multiplexer_1_out), .sel(in_9));
  Multiplexer #(.width(8), .enable("false")) multiplexer_2 (
    .in0(in_7), .in1({8{1'b0}}), .out(multiplexer_2_out), .sel(in_9));
  Multiplexer #(.width(13), .enable("false")) multiplexer_3 (
    .in0(in_8), .in1({13{1'b0}}), .out(multiplexer_3_out), .sel(in_9));
  Register #(.width(32), .trigger("falling")) register_1 (.D(in_1), .Q(out_12), .clk(in_10), .clr(in_11));  // open: en
  Register #(.width(32), .trigger("falling")) register_2 (.D(in_2), .Q(out_13), .clk(in_10), .clr(in_11));  // open: en
  Register #(.width(32), .trigger("falling")) register_3 (.D(in_3), .Q(out_14), .clk(in_10), .clr(in_11));  // open: en
  Register #(.width(32), .trigger("falling")) register_4 (.D(in_4), .Q(out_15), .clk(in_10), .clr(in_11));  // open: en
  Register #(.width(32), .trigger("falling")) register_5 (.D(in_5), .Q(out_16), .clk(in_10), .clr(in_11));  // open: en
  Register #(.width(32), .trigger("falling")) register_6 (
    .D(multiplexer_1_out), .Q(out_17), .clk(in_10), .clr(in_11));  // open: en
  Register #(.trigger("falling")) register_7 (.D(multiplexer_2_out), .Q(out_18), .clk(in_10), .clr(in_11));  // open: en
  Register #(.width(13), .trigger("falling")) register_8 (
    .D(multiplexer_3_out), .Q(out_19), .clk(in_10), .clr(in_11));  // open: en

  assign out_20 = out_17;

  // Notes on the sheet:
  //   OF-EX LATCH
endmodule

module EX_MA_Latch (
  input  [31:0] in_1,
  input  [31:0] in_2,
  input  [31:0] in_3,
  input  [31:0] in_4,
  input  [3:0] in_5,
  input  in_6,
  input  in_7,
  output [31:0] out_8,
  output [31:0] out_9,
  output [31:0] out_10,
  output [31:0] out_11,
  output [3:0] out_12,
  output [31:0] out_13
);

  Register #(.width(32), .trigger("falling")) register_1 (.D(in_1), .Q(out_8), .clk(in_6), .clr(in_7));  // open: en
  Register #(.width(32), .trigger("falling")) register_2 (.D(in_2), .Q(out_9), .clk(in_6), .clr(in_7));  // open: en
  Register #(.width(32), .trigger("falling")) register_3 (.D(in_3), .Q(out_10), .clk(in_6), .clr(in_7));  // open: en
  Register #(.width(32), .trigger("falling")) register_4 (.D(in_4), .Q(out_11), .clk(in_6), .clr(in_7));  // open: en
  Register #(.width(4), .trigger("falling")) register_5 (.D(in_5), .Q(out_12), .clk(in_6), .clr(in_7));  // open: en

  assign out_13 = out_11;

  // Notes on the sheet:
  //   EX-MA LATCH
endmodule

module MA_RW_Latch (
  input  [31:0] in_1,
  input  [31:0] in_2,
  input  [31:0] in_3,
  input  [31:0] in_4,
  input  [2:0] in_5,
  input  in_6,
  input  in_7,
  output [31:0] out_8,
  output [31:0] out_9,
  output [31:0] out_10,
  output [31:0] out_11,
  output [2:0] out_12,
  output [31:0] out_13
);

  Register #(.width(32), .trigger("falling")) register_1 (.D(in_1), .Q(out_8), .clk(in_6), .clr(in_7));  // open: en
  Register #(.width(32), .trigger("falling")) register_2 (.D(in_2), .Q(out_9), .clk(in_6), .clr(in_7));  // open: en
  Register #(.width(32), .trigger("falling")) register_3 (.D(in_3), .Q(out_10), .clk(in_6), .clr(in_7));  // open: en
  Register #(.width(32), .trigger("falling")) register_4 (.D(in_4), .Q(out_11), .clk(in_6), .clr(in_7));  // open: en
  Register #(.width(3), .trigger("falling")) register_5 (.D(in_5), .Q(out_12), .clk(in_6), .clr(in_7));  // open: en

  assign out_13 = out_11;

  // Notes on the sheet:
  //   MA-RW LATCH
endmodule

module _1st_operand_conflict (
  input  [31:0] A,
  input  [31:0] B,
  output out_3
);

  wire and_1_out, and_3_out, comparator_1_eq, comparator_2_eq, comparator_3_eq, comparator_4_eq,
       comparator_5_eq, comparator_6_eq, comparator_7_eq, comparator_8_eq, comparator_9_eq, comparator_10_eq,
       comparator_11_eq, comparator_12_eq, comparator_13_eq, comparator_14_eq, comparator_15_eq,
       comparator_16_eq, comparator_17_eq;
  wire [3:0] multiplexer_1_out, multiplexer_2_out;

  Comparator #(.width(5), .mode("unsigned")) comparator_1 (
    .a(A[31:27]), .b(5'b01101), .eq(comparator_1_eq));  // open: gt, lt
  Comparator #(.width(5), .mode("unsigned")) comparator_2 (
    .a(A[31:27]), .b(5'b10010), .eq(comparator_2_eq));  // open: gt, lt
  Comparator #(.width(5), .mode("unsigned")) comparator_3 (
    .a(A[31:27]), .b(5'b10000), .eq(comparator_3_eq));  // open: gt, lt
  Comparator #(.width(5), .mode("unsigned")) comparator_4 (
    .a(A[31:27]), .b(5'b10001), .eq(comparator_4_eq));  // open: gt, lt
  Comparator #(.width(5), .mode("unsigned")) comparator_5 (
    .a(A[31:27]), .b(5'b10011), .eq(comparator_5_eq));  // open: gt, lt
  Comparator #(.width(5), .mode("unsigned")) comparator_6 (
    .a(A[31:27]), .b(5'b01000), .eq(comparator_6_eq));  // open: gt, lt
  Comparator #(.width(5), .mode("unsigned")) comparator_7 (
    .a(A[31:27]), .b(5'b01001), .eq(comparator_7_eq));  // open: gt, lt
  and and_1 (and_1_out, ~comparator_1_eq, ~comparator_2_eq, ~comparator_3_eq, ~comparator_4_eq, ~comparator_5_eq, ~comparator_6_eq, ~comparator_7_eq);  // AND_Gate
  Comparator #(.width(5), .mode("unsigned")) comparator_8 (
    .a(A[31:27]), .b(5'b10100), .eq(comparator_8_eq));  // open: gt, lt
  Multiplexer #(.width(4), .enable("false")) multiplexer_1 (
    .in0(A[21:18]), .in1(4'b1111), .out(multiplexer_1_out), .sel(comparator_8_eq));
  and and_2 (out_3, and_1_out, comparator_9_eq, and_3_out);
  Comparator #(.width(4), .mode("unsigned")) comparator_9 (
    .a(multiplexer_2_out), .b(multiplexer_1_out), .eq(comparator_9_eq));  // open: gt, lt
  Comparator #(.width(5), .mode("unsigned")) comparator_10 (
    .a(B[31:27]), .b(5'b01101), .eq(comparator_10_eq));  // open: gt, lt
  Comparator #(.width(5), .mode("unsigned")) comparator_11 (
    .a(B[31:27]), .b(5'b10010), .eq(comparator_11_eq));  // open: gt, lt
  Comparator #(.width(5), .mode("unsigned")) comparator_12 (
    .a(B[31:27]), .b(5'b10000), .eq(comparator_12_eq));  // open: gt, lt
  Comparator #(.width(5), .mode("unsigned")) comparator_13 (
    .a(B[31:27]), .b(5'b10001), .eq(comparator_13_eq));  // open: gt, lt
  Comparator #(.width(5), .mode("unsigned")) comparator_14 (
    .a(B[31:27]), .b(5'b00101), .eq(comparator_14_eq));  // open: gt, lt
  Comparator #(.width(5), .mode("unsigned")) comparator_15 (
    .a(B[31:27]), .b(5'b01111), .eq(comparator_15_eq));  // open: gt, lt
  Comparator #(.width(5), .mode("unsigned")) comparator_16 (
    .a(B[31:27]), .b(5'b10100), .eq(comparator_16_eq));  // open: gt, lt
  and and_3 (and_3_out, ~comparator_10_eq, ~comparator_11_eq, ~comparator_12_eq, ~comparator_13_eq, ~comparator_14_eq, ~comparator_15_eq, ~comparator_16_eq);  // AND_Gate
  Multiplexer #(.width(4), .enable("false")) multiplexer_2 (
    .in0(B[25:22]), .in1(4'b1111), .out(multiplexer_2_out), .sel(comparator_17_eq));
  Comparator #(.width(5), .mode("unsigned")) comparator_17 (
    .a(B[31:27]), .b(5'b10011), .eq(comparator_17_eq));  // open: gt, lt
endmodule

module _2nd_operand_conflict (
  input  [31:0] A,
  input  [31:0] B,
  output out_3
);

  wire and_1_out, and_3_out, comparator_1_eq, comparator_2_eq, comparator_3_eq, comparator_4_eq,
       comparator_5_eq, comparator_6_eq, comparator_7_eq, comparator_8_eq, comparator_9_eq, comparator_10_eq,
       comparator_11_eq, comparator_12_eq, comparator_13_eq, comparator_14_eq, comparator_15_eq,
       multiplexer_2_out, multiplexer_3_out, not_1_out;
  wire [3:0] multiplexer_1_out, multiplexer_4_out;

  Comparator #(.width(5), .mode("unsigned")) comparator_1 (
    .a(A[31:27]), .b(5'b01101), .eq(comparator_1_eq));  // open: gt, lt
  Comparator #(.width(5), .mode("unsigned")) comparator_2 (
    .a(A[31:27]), .b(5'b10010), .eq(comparator_2_eq));  // open: gt, lt
  Comparator #(.width(5), .mode("unsigned")) comparator_3 (
    .a(A[31:27]), .b(5'b10000), .eq(comparator_3_eq));  // open: gt, lt
  Comparator #(.width(5), .mode("unsigned")) comparator_4 (
    .a(A[31:27]), .b(5'b10001), .eq(comparator_4_eq));  // open: gt, lt
  Comparator #(.width(5), .mode("unsigned")) comparator_5 (
    .a(A[31:27]), .b(5'b10011), .eq(comparator_5_eq));  // open: gt, lt
  and and_1 (and_1_out, ~comparator_1_eq, ~comparator_2_eq, ~comparator_3_eq, ~comparator_4_eq, ~comparator_5_eq);  // AND_Gate
  Comparator #(.width(5), .mode("unsigned")) comparator_6 (
    .a(A[31:27]), .b(5'b01111), .eq(comparator_6_eq));  // open: gt, lt
  Multiplexer #(.width(4), .enable("false")) multiplexer_1 (
    .in0(A[17:14]), .in1(A[25:22]), .out(multiplexer_1_out), .sel(comparator_6_eq));
  not not_1 (not_1_out, comparator_6_eq);
  Comparator #(.width(4), .mode("unsigned")) comparator_7 (
    .a(multiplexer_4_out), .b(multiplexer_1_out), .eq(comparator_7_eq));  // open: gt, lt
  Multiplexer #(.enable("false")) multiplexer_2 (.in0(1'b1), .in1(1'b0), .out(multiplexer_2_out), .sel(A[26]));
  Multiplexer #(.enable("false")) multiplexer_3 (
    .in0(1'b1), .in1(multiplexer_2_out), .out(multiplexer_3_out), .sel(not_1_out));
  and and_2 (out_3, and_1_out, comparator_7_eq, multiplexer_3_out, and_3_out);
  Comparator #(.width(5), .mode("unsigned")) comparator_8 (
    .a(B[31:27]), .b(5'b01101), .eq(comparator_8_eq));  // open: gt, lt
  Comparator #(.width(5), .mode("unsigned")) comparator_9 (
    .a(B[31:27]), .b(5'b10010), .eq(comparator_9_eq));  // open: gt, lt
  Comparator #(.width(5), .mode("unsigned")) comparator_10 (
    .a(B[31:27]), .b(5'b10000), .eq(comparator_10_eq));  // open: gt, lt
  Comparator #(.width(5), .mode("unsigned")) comparator_11 (
    .a(B[31:27]), .b(5'b10001), .eq(comparator_11_eq));  // open: gt, lt
  Comparator #(.width(5), .mode("unsigned")) comparator_12 (
    .a(B[31:27]), .b(5'b00101), .eq(comparator_12_eq));  // open: gt, lt
  Comparator #(.width(5), .mode("unsigned")) comparator_13 (
    .a(B[31:27]), .b(5'b01111), .eq(comparator_13_eq));  // open: gt, lt
  Comparator #(.width(5), .mode("unsigned")) comparator_14 (
    .a(B[31:27]), .b(5'b10100), .eq(comparator_14_eq));  // open: gt, lt
  and and_3 (and_3_out, ~comparator_8_eq, ~comparator_9_eq, ~comparator_10_eq, ~comparator_11_eq, ~comparator_12_eq, ~comparator_13_eq, ~comparator_14_eq);  // AND_Gate
  Multiplexer #(.width(4), .enable("false")) multiplexer_4 (
    .in0(B[25:22]), .in1(4'b1111), .out(multiplexer_4_out), .sel(comparator_15_eq));
  Comparator #(.width(5), .mode("unsigned")) comparator_15 (
    .a(B[31:27]), .b(5'b10011), .eq(comparator_15_eq));  // open: gt, lt
endmodule

module Branch_Lock_Unit (
  input  isBranchTaken,
  output invalidateSignal
);


  assign invalidateSignal = isBranchTaken;
endmodule

module Forwarding_Unit (
  input  [31:0] OF_instruction,
  input  [31:0] EX_instruction,
  input  [31:0] MA_instruction,
  input  [31:0] RW_instruction,
  output RW_OF_1,
  output RW_OF_2,
  output RW_EX_1,
  output RW_EX_2,
  output RW_MA,
  output MA_EX_1,
  output MA_EX_2
);

  wire comparator_1_eq, n2nd_operand_conflict_4_out_3;

  _1st_operand_conflict u_1st_operand_conflict_1 (.A(OF_instruction), .B(RW_instruction), .out_3(RW_OF_1));
  _2nd_operand_conflict u_2nd_operand_conflict_1 (.A(OF_instruction), .B(RW_instruction), .out_3(RW_OF_2));
  _1st_operand_conflict u_1st_operand_conflict_2 (.A(EX_instruction), .B(RW_instruction), .out_3(RW_EX_1));
  _2nd_operand_conflict u_2nd_operand_conflict_2 (.A(EX_instruction), .B(RW_instruction), .out_3(RW_EX_2));
  _2nd_operand_conflict u_2nd_operand_conflict_3 (.A(MA_instruction), .B(RW_instruction), .out_3(RW_MA));
  _1st_operand_conflict u_1st_operand_conflict_3 (.A(EX_instruction), .B(MA_instruction), .out_3(MA_EX_1));
  _2nd_operand_conflict u_2nd_operand_conflict_4 (
    .A(EX_instruction), .B(MA_instruction), .out_3(n2nd_operand_conflict_4_out_3));
  Comparator #(.width(5), .mode("unsigned")) comparator_1 (
    .a(EX_instruction[31:27]), .b(5'b01111), .eq(comparator_1_eq));  // open: gt, lt
  Multiplexer #(.enable("false")) multiplexer_1 (
    .in0(n2nd_operand_conflict_4_out_3), .in1(1'b0), .out(MA_EX_2), .sel(comparator_1_eq));
endmodule

module Instruction_conflict (
  input  [31:0] A,
  input  [31:0] B,
  output out_3
);

  wire and_1_out, and_2_out, and_3_out, and_4_out, and_6_out, comparator_1_eq, comparator_2_eq,
       comparator_3_eq, comparator_4_eq, comparator_5_eq, comparator_6_eq, comparator_7_eq, comparator_8_eq,
       comparator_9_eq, comparator_10_eq, comparator_11_eq, comparator_12_eq, comparator_13_eq,
       comparator_14_eq, comparator_15_eq, comparator_16_eq, comparator_17_eq, comparator_18_eq,
       comparator_19_eq, multiplexer_3_out, not_1_out, not_2_out, or_1_out;
  wire [3:0] multiplexer_1_out, multiplexer_2_out, multiplexer_4_out;

  Comparator #(.width(5), .mode("unsigned")) comparator_1 (
    .a(A[31:27]), .b(5'b10100), .eq(comparator_1_eq));  // open: gt, lt
  Multiplexer #(.width(4), .enable("false")) multiplexer_1 (
    .in0(A[21:18]), .in1(4'b1111), .out(multiplexer_1_out), .sel(comparator_1_eq));
  Comparator #(.width(4), .mode("unsigned")) comparator_2 (
    .a(multiplexer_4_out), .b(multiplexer_1_out), .eq(comparator_2_eq));  // open: gt, lt
  Comparator #(.width(5), .mode("unsigned")) comparator_3 (
    .a(A[31:27]), .b(5'b01101), .eq(comparator_3_eq));  // open: gt, lt
  Comparator #(.width(5), .mode("unsigned")) comparator_4 (
    .a(A[31:27]), .b(5'b10010), .eq(comparator_4_eq));  // open: gt, lt
  Comparator #(.width(5), .mode("unsigned")) comparator_5 (
    .a(A[31:27]), .b(5'b10000), .eq(comparator_5_eq));  // open: gt, lt
  Comparator #(.width(5), .mode("unsigned")) comparator_6 (
    .a(A[31:27]), .b(5'b10001), .eq(comparator_6_eq));  // open: gt, lt
  Comparator #(.width(5), .mode("unsigned")) comparator_7 (
    .a(A[31:27]), .b(5'b10011), .eq(comparator_7_eq));  // open: gt, lt
  Comparator #(.width(5), .mode("unsigned")) comparator_8 (
    .a(A[31:27]), .b(5'b01000), .eq(comparator_8_eq));  // open: gt, lt
  Comparator #(.width(5), .mode("unsigned")) comparator_9 (
    .a(A[31:27]), .b(5'b01001), .eq(comparator_9_eq));  // open: gt, lt
  and and_1 (and_1_out, ~comparator_3_eq, ~comparator_4_eq, ~comparator_5_eq, ~comparator_6_eq, ~comparator_7_eq);  // AND_Gate
  and and_2 (and_2_out, ~comparator_8_eq, ~comparator_9_eq);  // AND_Gate
  and and_3 (and_3_out, comparator_2_eq, and_2_out);
  Multiplexer #(.width(4), .enable("false")) multiplexer_2 (
    .in0(A[17:14]), .in1(A[25:22]), .out(multiplexer_2_out), .sel(comparator_10_eq));
  not not_1 (not_1_out, A[26]);
  Comparator #(.width(5), .mode("unsigned")) comparator_10 (
    .a(A[31:27]), .b(5'b01111), .eq(comparator_10_eq));  // open: gt, lt
  not not_2 (not_2_out, comparator_10_eq);
  Comparator #(.width(4), .mode("unsigned")) comparator_11 (
    .a(multiplexer_4_out), .b(multiplexer_2_out), .eq(comparator_11_eq));  // open: gt, lt
  Multiplexer #(.enable("false")) multiplexer_3 (.in0(1'b1), .in1(not_1_out), .out(multiplexer_3_out), .sel(not_2_out));
  and and_4 (and_4_out, comparator_11_eq, multiplexer_3_out);
  or or_1 (or_1_out, and_3_out, and_4_out);
  and and_5 (out_3, and_1_out, or_1_out, and_6_out);
  Comparator #(.width(5), .mode("unsigned")) comparator_12 (
    .a(B[31:27]), .b(5'b01101), .eq(comparator_12_eq));  // open: gt, lt
  Comparator #(.width(5), .mode("unsigned")) comparator_13 (
    .a(B[31:27]), .b(5'b10010), .eq(comparator_13_eq));  // open: gt, lt
  Comparator #(.width(5), .mode("unsigned")) comparator_14 (
    .a(B[31:27]), .b(5'b10000), .eq(comparator_14_eq));  // open: gt, lt
  Comparator #(.width(5), .mode("unsigned")) comparator_15 (
    .a(B[31:27]), .b(5'b10001), .eq(comparator_15_eq));  // open: gt, lt
  Comparator #(.width(5), .mode("unsigned")) comparator_16 (
    .a(B[31:27]), .b(5'b00101), .eq(comparator_16_eq));  // open: gt, lt
  Comparator #(.width(5), .mode("unsigned")) comparator_17 (
    .a(B[31:27]), .b(5'b01111), .eq(comparator_17_eq));  // open: gt, lt
  Comparator #(.width(5), .mode("unsigned")) comparator_18 (
    .a(B[31:27]), .b(5'b10100), .eq(comparator_18_eq));  // open: gt, lt
  and and_6 (and_6_out, ~comparator_12_eq, ~comparator_13_eq, ~comparator_14_eq, ~comparator_15_eq, ~comparator_16_eq, ~comparator_17_eq, ~comparator_18_eq);  // AND_Gate
  Comparator #(.width(5), .mode("unsigned")) comparator_19 (
    .a(B[31:27]), .b(5'b10011), .eq(comparator_19_eq));  // open: gt, lt
  Multiplexer #(.width(4), .enable("false")) multiplexer_4 (
    .in0(B[25:22]), .in1(4'b1111), .out(multiplexer_4_out), .sel(comparator_19_eq));

  // Notes on the sheet:
  //   src1
  //   hasSrc1
  //   src2
  //   hasSrc2
  //   dest
endmodule

module Data_Lock_Unit (
  input  [31:0] OF_instruction,
  input  [31:0] EX_instruction,
  output Stall
);

  wire comparator_1_eq, instruction_conflict_1_out_3;

  Comparator #(.width(5), .mode("unsigned")) comparator_1 (
    .a(EX_instruction[31:27]), .b(5'b01110), .eq(comparator_1_eq));  // open: gt, lt
  Instruction_conflict instruction_conflict_1 (
    .A(OF_instruction), .B(EX_instruction), .out_3(instruction_conflict_1_out_3));
  Multiplexer #(.enable("false")) multiplexer_1 (
    .in0(1'b0), .in1(instruction_conflict_1_out_3), .out(Stall), .sel(comparator_1_eq));
endmodule
